# Fritzing sketch proto1 (saved by Fritzing 0.9.3b)
perfboards: 1

parts:
  부품1 = Arduino Micro (Rev3)
  IR1 = TSOP312.., 314.. [package=THT]
  부품2 = InvenSense MPU6050
  L298N1 = L298N DC motor driver
  DC_Mot_Enc1 = DC Motor with two-phase hall-encoder [part_number=VT-E-G25A-06-177E]  # not connected
  DC_Mot_Enc2 = DC Motor with two-phase hall-encoder [part_number=VT-E-G25A-06-177E]  # not connected

nets:
  GND: 부품1.GND, IR1.Vs, 부품2.GND, L298N1.GND
  VIN: 부품1.VIN, L298N1.5V
  5V: 부품1.5V, IR1.Data, 부품2.VCC
  N1: 부품1.A5, 부품2.SCL
  N2: 부품1.A4, 부품2.SDA
  N3: 부품1.A3, IR1.GND

custom parts:
  L298N DC motor driver: 2x DC motor driver with 78M05 positive voltage regulator (7..35 V) L298N: max 46 V, 2 A Set 5 V Enable jumper to enable 5 V regultor (needed for the L298N) and +5 V output at screw terminal or supply external +5 V at screw terminal Set ENA and/or ENB to +5 V to enable motor permanently or supply ENA and/or ENB with PWM signal IN1 and IN2 set rotation directory for motor A (OUT1/OUT2) IN2 and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
