# Fritzing sketch proto1 (saved by Fritzing 0.9.3b)

parts:
  부품1 = Arduino Uno (Rev3)
  부품2 = Bluetooth HC-05 Macho
  L298N1 = L298N DC motor driver
  부품3 = InvenSense MPU6050
  DC_Mot_Enc1 = DC Motor with two-phase hall-encoder [part_number=VT-E-G25A-06-177E]
  DC_Mot_Enc2 = DC Motor with two-phase hall-encoder [part_number=VT-E-G25A-06-177E]
  IR1 = TSOP312.., 314.. [package=THT]

nets:
  N1: 부품1.A3, IR1.GND
  N2: 부품1.A4/SDA, 부품3.SDA, 부품3.XDA
  N3: 부품1.A5/SCL, 부품3.SCL
  N4: 부품1.D8, L298N1.IN1
  N5: 부품1.D9_PWM, L298N1.5V#10, L298N1.ENB
  N6: 부품1.D10_PWM/SS, L298N1.5V#9, L298N1.ENA
  N7: 부품1.D11_PWM/MOSI, DC_Mot_Enc1.pin5
  N8: 부품1.D12/MISO, 부품2.RXD
  N9: 부품1.D13/SCK, 부품2.TXD
  GND: 부품1.GND, 부품2.GND, L298N1.GND, 부품3.GND, DC_Mot_Enc1.pin4, DC_Mot_Enc2.pin4, IR1.Vs
  N10: 부품1.D2, DC_Mot_Enc2.pin6
  N11: 부품1.D3_PWM, DC_Mot_Enc1.pin6
  N12: 부품1.D4, DC_Mot_Enc2.pin5
  N13: 부품1.D5_PWM, L298N1.IN4
  N14: 부품1.D6_PWM, L298N1.IN3
  N15: 부품1.D7, L298N1.IN2
  VCC: 부품1.5V, 부품2.VCC, 부품3.VCC, DC_Mot_Enc1.pin3, DC_Mot_Enc2.pin3, IR1.Data
  N16: 부품1.VIN, L298N1.5V#7
  N17: L298N1.OUT1, DC_Mot_Enc1.pin2
  N18: L298N1.OUT2, DC_Mot_Enc1.pin1
  N19: L298N1.OUT3, DC_Mot_Enc2.pin2
  N20: L298N1.OUT4, DC_Mot_Enc2.pin1

custom parts:
  L298N DC motor driver: 2x DC motor driver with 78M05 positive voltage regulator (7..35 V) L298N: max 46 V, 2 A Set 5 V Enable jumper to enable 5 V regultor (needed for the L298N) and +5 V output at screw terminal or supply external +5 V at screw terminal Set ENA and/or ENB to +5 V to enable motor permanently or supply ENA and/or ENB with PWM signal IN1 and IN2 set rotation directory for motor A (OUT1/OUT2) IN2 and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
