# Fritzing sketch proto2 (saved by Fritzing 0.9.9b)
circuit board: 8.31533cm x 8.46322cm

parts:
  부품2 = InvenSense MPU6050
  Pololu_A2 = Pololu A4988 [package=SO16]
  IR1 = TSOP312.., 314.. [package=THT]
  C1 = Electrolytic Capacitor [capacitance=100μF voltage=35V package="0807 [SMD, electrolytic]"]
  M1 = Stepper Motor - Unipolar
  M2 = Stepper Motor - Unipolar
  Pololu_A1 = Pololu A4988 [package=SO16]
  S1 = Taiway 100-SP-X-T1 SPDT Miniature Toggle Switch [part_number=100-SP-X-T1-0-0-B1-M2 package=THT]
  부품1 = Arduino Nano (Rev3.0) (ICSP)
  BAT1 = Battery Holders [package=lipo-1100mAh]

nets:
  VDD: 부품2.VCC, Pololu_A2.MS1, Pololu_A2.MS2, Pololu_A2.MS3, Pololu_A2.VDD, IR1.Data, Pololu_A1.MS1, Pololu_A1.MS2, Pololu_A1.MS3, Pololu_A1.VDD, 부품1.5V
  GND: 부품2.GND, Pololu_A2.GND, IR1.Vs, C1.-, Pololu_A1.GND, 부품1.GND, BAT1.-
  N1: 부품2.SCL, 부품1.A5
  N2: 부품2.SDA, 부품1.A4
  N3: Pololu_A2.ENABLE, 부품1.D10
  N4: Pololu_A2.RESET, Pololu_A2.SLEEP
  N5: Pololu_A2.STEP, 부품1.D9
  N6: Pololu_A2.DIR, 부품1.D8
  N7: Pololu_A2.1B, M2.D
  N8: Pololu_A2.1A, M2.B
  N9: Pololu_A2.2A, M2.C
  N10: Pololu_A2.2B, M2.A
  N11: Pololu_A2.VMOT, C1.+, Pololu_A1.VMOT, S1.L1, 부품1.VIN
  N12: IR1.GND, 부품1.A3
  N13: M1.A, Pololu_A1.2B
  N14: M1.C, Pololu_A1.2A
  N15: M1.B, Pololu_A1.1A
  N16: M1.D, Pololu_A1.1B
  N17: Pololu_A1.ENABLE, 부품1.D7
  N18: Pololu_A1.RESET, Pololu_A1.SLEEP
  N19: Pololu_A1.STEP, 부품1.D6
  N20: Pololu_A1.DIR, 부품1.D5
  N21: S1.COM, BAT1.+
